# Fritzing sketch schematic (saved by Fritzing 1.0.4)

parts:
  L298N1 = L298N DC motor driver
  M3 = DC Motor [voltage_(max)=6V voltage_(min)=3V]
  M4 = DC Motor [voltage_(max)=6V voltage_(min)=3V]
  Part1 = Arduino Uno (Rev3) - ICSP
  GY1 = MPU-6050 Board GY-521 [form="♀ (female)" package=THT]
  A2 = tf-luna lidar
  M5 = bb-usb-cable [package=THT]  # not connected
  M6 = RioRand LM2596
  M7 = bb-usb-cable [package=THT]  # not connected
  Mod1 = generic-ac-power-supply [package=THT]
  J1 = Power Jack [package=power_jack_combo]
  R1 = Resistor [tolerance=±5% resistance=470 package="0603 [SMD]"]
  R2 = Resistor [tolerance=±5% resistance=470 package="0603 [SMD]"]
  R3 = Resistor [tolerance=±5% resistance=330 package="0603 [SMD]"]
  R4 = Resistor [tolerance=±5% resistance=330 package="0603 [SMD]"]
  R5 = Resistor [tolerance=±5% resistance=330 package="0603 [SMD]"]
  R6 = Resistor [tolerance=±5% resistance=330 package="0603 [SMD]"]
  LED1 = RGB LED (com. cathode, rgb) [color="Red (633nm)" current=0.030A package="5 mm [THT]"]
  LED2 = RGB LED (com. cathode, rgb) [color="Red (633nm)" current=0.030A package="5 mm [THT]"]
  A3 = Treedix Screw Terminal Block Breakout Module
  M8 = Stepper Motor - Unipolar  # not connected
  M9 = Stepper Motor - Unipolar
  Driver1 = 28BYJ-48 Driver Module [part_number=ULN2003 package=THT]
  Mod2 = Raspberry Pi 4B  # not connected

nets:
  N1: L298N1.OUT1, M3.pin_2
  N2: L298N1.OUT2, M3.pin_1
  N3: L298N1.OUT3, M4.pin_2
  N4: L298N1.OUT4, M4.pin_1
  GND: L298N1.12V, L298N1.GND, Part1.D10_PWM/SS, GY1.pin2, A2.Pin_4, A2.Pin_5, M6.Pin_1, M6.Pin_2, M6.Pin_4, J1.PWR, LED1.common_cathode, LED2.common_cathode, A3.Pin_45, A3.Pin_46, A3.Pin_47, A3.Pin_48, A3.Pin_49, A3.Pin_60, A3.Pin_112, Driver1.GND
  N5: L298N1.5V, Part1.AREF, GY1.pin1, A2.Pin_1, M6.Pin_3, A3.Pin_50, A3.Pin_55, A3.Pin_56, A3.Pin_62, Driver1.Vmotor
  N6: L298N1.ENA, A3.Pin_73, A3.Pin_107
  N7: L298N1.ENB, A3.Pin_74, A3.Pin_108
  N8: L298N1.IN1, A3.Pin_65
  N9: L298N1.IN2, Part1.ICSP2_MOSI, Part1.GND, A3.Pin_67, A3.Pin_84, A3.Pin_102
  N10: L298N1.IN3, A3.Pin_70
  N11: L298N1.IN4, A3.Pin_72, A3.Pin_106
  N12: Part1.ICSP2_SCK, Part1.RESET2, R1.Pin_0, A3.Pin_66, A3.Pin_83, A3.Pin_101
  N13: Part1.3V3, A3.Pin_71, A3.Pin_113
  N14: GY1.pin3, A2.Pin_3, A3.Pin_14, A3.Pin_79
  N15: GY1.pin4, A2.Pin_2, A3.Pin_35, A3.Pin_78
  N16: Mod1.pin3#2, J1.GND
  N17: Mod1.pin3#3, J1.GNDBREAK
  N18: R1.Pin_1, LED2.red_anode
  N19: R2.Pin_0, A3.Pin_61, A3.Pin_75
  N20: R2.Pin_1, LED1.red_anode
  N21: R3.Pin_0, A3.Pin_68
  N22: R3.Pin_1, LED2.green_anode
  N23: R4.Pin_0, A3.Pin_69
  N24: R4.Pin_1, LED2.blue_anode
  N25: R5.Pin_0, A3.Pin_59, A3.Pin_76
  N26: R5.Pin_1, LED1.green_anode
  N27: R6.Pin_0, A3.Pin_58, A3.Pin_77
  N28: R6.Pin_1, LED1.blue_anode
  N29: A3.Pin_31, Driver1.IN1
  N30: A3.Pin_32, Driver1.IN2
  N31: A3.Pin_33, Driver1.IN3
  N32: A3.Pin_34, Driver1.IN4
  N33: M9.A, M9.D, Driver1.blue-pin
  N34: M9.COMMON_1, Driver1.pink-pin
  N35: M9.C, Driver1.yellow-pin
  N36: M9.B, Driver1.orange-pin
  N37: M9.COMMON_2, Driver1.red-pin

notes:
  R(VIN+),W(SDA),B(SCL),G(GND),Y(I2CMode),Black(unused)

custom parts:
  L298N DC motor driver: 2x DC motor driver with 78M05 positive voltage regulator (7..35 V) L298N: max 46 V, 2 A Set 5 V Enable jumper to enable 5 V regultor (needed for the L298N) and +5 V output at screw terminal or supply external +5 V at screw terminal Set ENA and/or ENB to +5 V to enable motor permanently or supply ENA and/or ENB with PWM signal IN1 and IN2 set rotation directory for motor A (OUT1/OUT2) IN2 and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
  MPU-6050 Board GY-521: Acelerometro y Giroscopio MPU-6050 Board GY-521
  tf-luna lidar: TF-Luna is using Time of Flight (TOF) principle to measure distance, and it periodically emits near infrared modulated wave.
  bb-usb-cable: Breadboard only, no connectors USB cable for the Raspberry PIs.
  generic-ac-power-supply: Generic ac power supply module. Use as is, or customize the svgs to fit your particular device (as they are all different.) Provides AC input and single DC output. PCB is generic and will need modifications if you intend to do a pcb mount.
  Treedix Screw Terminal Block Breakout Module: Treedix Screw Terminal Block Breakout Module.
  28BYJ-48 Driver Module: ULN2003 Driver Module for the 28BYJ-48 Unipolar Stepper Motor LED A - Blue wire - Bottom coil left LED B - Pink wire - Top coil left LED C - Yellow wire - Bottom coil right LED D - Orange wire - Top coil right Common rail - red Connector pins: blue - pink - yellow - orange - red Control pins - IN1 to IN4 Power pins - GND & Vmotor (5-12V) On/Off jumper (if removed, power to motor is cut).
